// Logisim project ROMTest.circ as structural Verilog: 1 circuit, main circuit main
module main (
  input  NMREQ,
  input  A13,
  input  NWR,
  input  NIORQ,
  input  A15,
  input  WRITESEL,
  input  A12,
  input  D7,
  input  NRESET,
  input  NROMEN,
  input  ROMDIS
);

  wire and_1_out, n7474_1_pin4, n7474_1_pin5, n7474_1_pin8, n7474_1_pin10, nor_1_out, nor_2_out, or_1_out,
       or_2_out, or_3_out, or_4_out, or_5_out, or_6_out;

  or or_1 (or_1_out, NWR, NIORQ);
  or or_2 (or_2_out, A13, or_1_out);
  nor nor_1 (nor_1_out, A15, n7474_1_pin5);
  or or_3 (or_3_out, or_2_out, A12);
  // Probe on or_2_out
  // Probe on nor_1_out
  _7474 u_7474_1 (
    .pin1(NRESET), .pin2(D7), .pin3(or_3_out), .pin4(n7474_1_pin4), .pin5(n7474_1_pin5),
    .pin13(n7474_1_pin5), .pin12(WRITESEL), .pin11(or_3_out), .pin10(n7474_1_pin10), .pin8(n7474_1_pin8));  // open: pin6, pin9
  // Probe on n7474_1_pin8
  // Probe on n7474_1_pin5
  or or_4 (or_4_out, NMREQ, or_5_out);
  or or_5 (or_5_out, NWR, n7474_1_pin8);
  or or_6 (or_6_out, NROMEN, ROMDIS);
  // Probe on or_4_out
  // Probe on and_1_out
  and and_1 (and_1_out, or_4_out, or_6_out);
  // Probe on nor_2_out
  nor nor_2 (nor_2_out, or_4_out, or_4_out);
  // also tied to VCC on the sheet: {n7474_1_pin4, n7474_1_pin10}
endmodule
